// Logisim project 4bitalunew.circ as structural Verilog: 1 circuit, main circuit onebitalu
module onebitalu (
  input  CONTROL,
  input  B0,
  input  B1,
  input  B2,
  input  B3,
  input  A0,
  input  A1,
  input  A2,
  input  A3,
  input  S2,
  input  S1,
  input  S0
);

  wire and_1_out, and_2_out, and_3_out, and_4_out, and_5_out, and_6_out, and_7_out, and_8_out, and_9_out,
       and_10_out, and_11_out, and_12_out, and_13_out, and_14_out, and_15_out, and_16_out, and_17_out,
       and_18_out, and_19_out, and_20_out, and_21_out, and_22_out, and_23_out, and_24_out, and_25_out,
       and_26_out, and_27_out, and_28_out, and_29_out, and_30_out, and_31_out, and_32_out, and_33_out,
       nor_1_out, not_1_out, not_2_out, not_3_out, not_4_out, not_5_out, not_6_out, not_7_out, not_8_out,
       not_9_out, or_1_out, or_2_out, or_3_out, or_4_out, or_5_out, or_6_out, or_7_out, or_8_out, or_9_out,
       or_10_out, or_11_out, or_12_out, or_13_out, or_14_out, or_15_out, or_16_out, or_17_out, or_18_out,
       or_19_out, or_20_out, or_21_out, or_22_out, or_23_out, or_24_out, xor_1_out, xor_2_out, xor_3_out,
       xor_4_out, xor_5_out, xor_6_out, xor_7_out, xor_8_out, xor_9_out, xor_10_out, xor_11_out, xor_12_out,
       xor_13_out, xor_14_out, xor_15_out, xor_16_out, xor_17_out, xor_18_out;

  xor xor_1 (xor_1_out, B0, CONTROL);
  xor xor_2 (xor_2_out, B1, CONTROL);
  xor xor_3 (xor_3_out, B2, CONTROL);
  xor xor_4 (xor_4_out, B3, CONTROL);
  xor xor_5 (xor_5_out, A0, xor_1_out);
  xor xor_6 (xor_6_out, A1, xor_2_out);
  and and_1 (and_1_out, xor_2_out, A1);
  xor xor_7 (xor_7_out, A2, xor_3_out);
  xor xor_8 (xor_8_out, A3, xor_4_out);
  and and_2 (and_2_out, xor_1_out, A0);
  and and_3 (and_3_out, xor_3_out, A2);
  and and_4 (and_4_out, xor_4_out, A3);
  and and_5 (and_5_out, xor_5_out, CONTROL);
  not not_1 (not_1_out, A0);
  xor xor_9 (xor_9_out, xor_6_out, or_4_out);
  and and_6 (and_6_out, xor_6_out, or_4_out);
  and and_7 (and_7_out, A1, B1);
  or or_1 (or_1_out, A1, B1);
  not not_2 (not_2_out, A1);
  xor xor_10 (xor_10_out, xor_7_out, or_6_out);
  and and_8 (and_8_out, xor_7_out, or_6_out);
  and and_9 (and_9_out, A2, B2);
  or or_2 (or_2_out, A2, B2);
  not not_3 (not_3_out, A2);
  xor xor_11 (xor_11_out, xor_8_out, or_7_out);
  and and_10 (and_10_out, xor_8_out, or_7_out);
  and and_11 (and_11_out, A3, B3);
  or or_3 (or_3_out, A3, B3);
  not not_4 (not_4_out, A3);
  xor xor_12 (xor_12_out, xor_5_out, CONTROL);
  or or_4 (or_4_out, and_2_out, and_5_out);
  and and_12 (and_12_out, A0, B0);
  or or_5 (or_5_out, A0, B0);
  xor xor_13 (xor_13_out, A0, B0);
  or or_6 (or_6_out, and_1_out, and_6_out);
  xor xor_14 (xor_14_out, A1, B1);
  or or_7 (or_7_out, and_3_out, and_8_out);
  xor xor_15 (xor_15_out, A2, B2);
  or or_8 (or_8_out, and_4_out, and_10_out);
  xor xor_16 (xor_16_out, A3, B3);
  // Probe on not_5_out
  not not_5 (not_5_out, or_8_out);
  // Probe on or_8_out
  not not_6 (not_6_out, S2);
  not not_7 (not_7_out, S1);
  not not_8 (not_8_out, S0);
  and and_13 (and_13_out, xor_12_out, not_6_out, not_7_out, not_8_out);
  and and_14 (and_14_out, and_12_out, not_6_out, not_7_out, S0);
  and and_15 (and_15_out, or_5_out, not_6_out, S1, not_8_out);
  and and_16 (and_16_out, not_1_out, not_6_out, S1, S0);
  and and_17 (and_17_out, xor_13_out, S2, not_7_out, not_8_out);
  and and_18 (and_18_out, xor_9_out, not_6_out, not_7_out, not_8_out);
  and and_19 (and_19_out, and_7_out, not_6_out, not_7_out, S0);
  and and_20 (and_20_out, or_1_out, not_6_out, S1, not_8_out);
  and and_21 (and_21_out, not_2_out, not_6_out, S1, S0);
  and and_22 (and_22_out, xor_14_out, S2, not_7_out, not_8_out);
  and and_23 (and_23_out, xor_10_out, not_6_out, not_7_out, not_8_out);
  and and_24 (and_24_out, and_9_out, not_6_out, not_7_out, S0);
  and and_25 (and_25_out, or_2_out, not_6_out, S1, not_8_out);
  and and_26 (and_26_out, not_3_out, not_6_out, S1, S0);
  and and_27 (and_27_out, xor_15_out, S2, not_7_out, not_8_out);
  and and_28 (and_28_out, xor_11_out, not_6_out, not_7_out, not_8_out);
  and and_29 (and_29_out, and_11_out, not_6_out, not_7_out, S0);
  and and_30 (and_30_out, or_3_out, not_6_out, S1, not_8_out);
  and and_31 (and_31_out, not_4_out, not_6_out, S1, S0);
  and and_32 (and_32_out, xor_16_out, S2, not_7_out, not_8_out);
  or or_9 (or_9_out, and_13_out, and_14_out);
  or or_10 (or_10_out, and_16_out, and_17_out);
  or or_11 (or_11_out, and_18_out, and_19_out);
  or or_12 (or_12_out, and_21_out, and_22_out);
  or or_13 (or_13_out, and_23_out, and_24_out);
  or or_14 (or_14_out, and_26_out, and_27_out);
  or or_15 (or_15_out, and_28_out, and_29_out);
  or or_16 (or_16_out, and_31_out, and_32_out);
  or or_17 (or_17_out, or_9_out, and_15_out);
  or or_18 (or_18_out, or_11_out, and_20_out);
  or or_19 (or_19_out, or_13_out, and_25_out);
  or or_20 (or_20_out, or_15_out, and_30_out);
  or or_21 (or_21_out, or_17_out, or_10_out);
  or or_22 (or_22_out, or_18_out, or_12_out);
  or or_23 (or_23_out, or_19_out, or_14_out);
  or or_24 (or_24_out, or_20_out, or_16_out);
  // Probe on or_22_out
  // Probe on or_23_out
  // Probe on or_24_out
  // Probe on or_21_out
  xor xor_17 (xor_17_out, A3, xor_4_out);
  // Probe on nor_1_out
  nor nor_1 (nor_1_out, or_21_out, or_24_out, or_23_out, or_22_out);
  not not_9 (not_9_out, xor_17_out);
  xor xor_18 (xor_18_out, A3, xor_11_out);
  // Probe on and_33_out
  and and_33 (and_33_out, xor_18_out, not_9_out);
endmodule
